// Logisim project Ctl_Load_Store.circ as structural Verilog: 1 circuit, main circuit Load_Store
module Load_Store (
  input  [31:0] Stack_Pointer,
  input  Enable,
  input  [15:0] Instruction,
  input  Clk,
  input  Reset,
  output [31:0] RAM_Addr,
  output [2:0] Rmd,
  output Store,
  output Load,
  output PC_Hold
);

  wire and_1_out, d_ff_1_q, d_ff_1_qn, not_1_out;
  wire [31:0] adder_1_out, bit_extender_1_out, bit_extender_2_out;

  D_Flip_Flop d_ff_1 (.D(and_1_out), .clk(Clk), .Q(d_ff_1_q), .Qn(d_ff_1_qn), .preset(1'b0), .reset(Reset));
  and and_1 (and_1_out, Enable, d_ff_1_qn);
  assign bit_extender_1_out = {{24{Instruction[7]}}, Instruction[7:0]};  // Bit_Extender bit_extender_1
  Multiplexer #(.enable("false"), .width(3)) multiplexer_1 (
    .in0(3'b000), .in1(Instruction[10:8]), .out(Rmd), .sel(Enable));
  and and_2 (Store, Enable, not_1_out);
  not not_1 (not_1_out, Instruction[11]);
  and and_3 (Load, Instruction[11], d_ff_1_q, Enable);
  and and_4 (PC_Hold, d_ff_1_qn, Enable);
  assign bit_extender_2_out = {{31{Enable}}, Enable};  // Bit_Extender bit_extender_2
  assign RAM_Addr = bit_extender_2_out & adder_1_out;  // AND_Gate and_5, 32 bits wide
  Adder #(.width(32)) adder_1 (.a(Stack_Pointer), .b(bit_extender_1_out), .out(adder_1_out));  // open: cin, cout

  // Notes on the sheet:
  //   Instruction: pull=down
endmodule
